// Logisim project custom_reg.circ as structural Verilog: 12 circuits, main circuit Register
module Register (
  input  [31:0] Data_In,
  input  Load,
  input  Clock,
  output [31:0] Data_out
);

  Register_part #(.width(32)) register_1 (.D(Data_In), .en(Load), .Q(Data_out), .clk(Clock));  // open: clr
endmodule

// BusReg
module BusRegister (
  input  [31:0] Data_In,
  input  Load,
  input  Clock,
  input  Bus,
  output [31:0] Data_out,
  output [31:0] Bus_out
);

  Register_part #(.width(32)) register_1 (.D(Data_In), .en(Load), .Q(Data_out), .clk(Clock));  // open: clr
  assign Bus_out = Bus ? Data_out : 32'bz;  // Controlled_Buffer controlled_buffer_1
endmodule

// ClearReg
module ClearRegister (
  input  [31:0] Data_In,
  input  Load,
  input  Clock,
  input  Clear,
  input  Bus,
  output [31:0] Data_out,
  output [31:0] Bus_out
);

  Register_part #(.width(32)) register_1 (.D(Data_In), .en(Load), .Q(Data_out), .clk(Clock), .clr(Clear));
  assign Bus_out = Bus ? Data_out : 32'bz;  // Controlled_Buffer controlled_buffer_1
endmodule

// CountReg
module CountRegister (
  input  [31:0] Data_In,
  input  Count,
  input  Load,
  input  Clock,
  input  Bus,
  output [31:0] Data_out,
  output [31:0] Bus_out
);

  wire or_1_out;
  wire [31:0] adder_1_out, multiplexer_1_out;

  Adder #(.width(32)) adder_1 (.a(Data_out), .b(32'h1), .out(adder_1_out));  // open: cin, cout
  Multiplexer #(.width(32), .enable("false")) multiplexer_1 (
    .in0(Data_In), .in1(adder_1_out), .out(multiplexer_1_out), .sel(Count));
  or or_1 (or_1_out, Count, Load);
  Register_part #(.width(32)) register_1 (
    .D(multiplexer_1_out), .en(or_1_out), .Q(Data_out), .clk(Clock));  // open: clr
  assign Bus_out = Bus ? Data_out : 32'bz;  // Controlled_Buffer controlled_buffer_1
endmodule

module ACC (
  input  [31:0] Data_In,
  input  load,
  input  clock,
  input  clear,
  input  bus,
  output [31:0] Data_out,
  output [31:0] Data_out_2
);

  ClearRegister clearregister_1 (
    .Data_In(Data_In), .Load(load), .Clock(clock), .Clear(clear), .Bus(bus), .Data_out(Data_out),
    .Bus_out(Data_out_2));
endmodule

module AR (
  input  [31:0] Data_In,
  input  load,
  input  clock,
  output [31:0] Data_out
);

  Register register_1 (.Data_In(Data_In), .Load(load), .Clock(clock), .Data_out(Data_out));
endmodule

module DR (
  input  [31:0] Data_In,
  input  load,
  input  clock,
  input  bus,
  output [31:0] Data_out,
  output [31:0] Data_out_2
);

  BusRegister busregister_1 (
    .Data_In(Data_In), .Load(load), .Clock(clock), .Bus(bus), .Data_out(Data_out), .Bus_out(Data_out_2));
endmodule

module IR (
  input  [31:0] Data_In,
  input  load,
  input  clock,
  output [31:0] Data_out
);

  Register register_1 (.Data_In(Data_In), .Load(load), .Clock(clock), .Data_out(Data_out));
endmodule

module OUTR (
  input  [31:0] Data_In,
  input  load,
  input  clock,
  output [31:0] Data_out
);

  Register register_1 (.Data_In(Data_In), .Load(load), .Clock(clock), .Data_out(Data_out));
endmodule

module PC (
  input  [31:0] Data_In,
  input  count,
  input  load,
  input  clock,
  input  bus,
  output [31:0] Data_out,
  output [31:0] Data_out_2
);

  CountRegister countregister_1 (
    .Data_In(Data_In), .Count(count), .Load(load), .Clock(clock), .Bus(bus), .Data_out(Data_out),
    .Bus_out(Data_out_2));
endmodule

module R (
  input  [31:0] Data_In,
  input  load,
  input  clock,
  input  bus,
  output [31:0] Data_out,
  output [31:0] Data_out_2
);

  BusRegister busregister_1 (
    .Data_In(Data_In), .Load(load), .Clock(clock), .Bus(bus), .Data_out(Data_out), .Bus_out(Data_out_2));
endmodule

module _1_bit_reg (
  input  Clock,
  input  Data,
  input  Clear,
  input  Load,
  output Data_out
);

  wire and_1_out, and_2_out, not_1_out, not_2_out;

  and and_1 (and_1_out, Data, Load);
  not not_1 (not_1_out, Data);
  and and_2 (and_2_out, not_1_out, Load);
  J_K_Flip_Flop j_k_ff_1 (
    .J(and_1_out), .clk(Clock), .K(and_2_out), .Q(Data_out), .preset(1'b0), .en(not_2_out), .reset(Clear));  // open: Qn
  not not_2 (not_2_out, Clear);

  // Notes on the sheet:
  //   Josiah Rininger
  //   OLA 5
  //   1bit_reg
endmodule
